# Fritzing sketch wiring_and_assembly (saved by Fritzing 0.9.4)

parts:
  S1 = H-Bridge with L298N
  M1 = DOIT Esp32 DevKit v1 (30 pins long, 11 pins width) [part_number=ESP32S-PIN30]
  VCC1 = 4 x AAA Battery Mount
  Reg1 = DC-DC CONVERTER [part_number=80633 package=dc-dc_converter]
  U1 = Luxeon LED [package=luxeon]
  U2 = Luxeon LED [package=luxeon]

nets:
  N1: S1.12V, Reg1.OUT+
  GND: S1.GND, M1.GND, Reg1.OUT-
  N2: S1.5V, VCC1.+, Reg1.IN+
  N3: S1.ENA, M1.D19
  N4: S1.IN1, M1.D18
  N5: S1.IN4, M1.TX2
  N6: S1.ENB, M1.RX2
  N7: S1.M1-01, U1.A
  N8: S1.M1-02, U1.C
  N9: S1.M2-01, U2.C
  N10: S1.M2-02, U2.A
  N11: VCC1.-, Reg1.IN-

notes:
  any 5V DC power supply
  Step-Up Module
  -> 5V DC in
  24V DC out ->
  Note:
  [In -] = [Out -]
  (GND in = GND out)
  (pins of this ESP32 are wrong/old)
  Correct ESP32 wiring:
  G19 -> ENA
  G18 -> IN1
  G17 -> IN4
  G16 -> ENB
  ESP32 devboard is powered via micro usb
  24V DC LED Lamp each
  for lower voltage lamps:
  decrease step-up module output voltage

custom parts:
  H-Bridge with L298N: h-bridge
  DOIT Esp32 DevKit v1 (30 pins long, 11 pins width): The DOIT Esp32 DevKit v1 is one of the development board created by DOIT to evaluate the ESP-WROOM-32 module. It is based on the ESP32 microcontroller that boasts Wifi, Bluetooth, Ethernet and Low Power support all in a single chip. (vanepp) made breadboard work, adjusted pin numbering and labels and reduced size of schematic and cleaned up pcb. This chip is 30pins long (2 x15) and 11 pins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
  DC-DC CONVERTER: WYHP 5A constant current/voltage manufactured by Shenzhen Weiyapuhua Technology Co., Ltd
